# Fritzing sketch EME (saved by Fritzing 0.9.4)
circuit board: 15.5673cm x 7.45374cm
breadboards: 1

parts:
  ▼ = Pushbutton [package="[THT]"]
  A = SWITCH-MOMENTARY-2 [package=tactile-pth-12mm]
  ▲ = Pushbutton [package="[THT]"]
  LCD1 = LCD screen
  S8 = Pushbutton [package="[THT]"]
  ◄ = Pushbutton [package="[THT]"]
  R2 = Resistor [tolerance=±5% resistance=100 package=THT]
  ► = Pushbutton [package="[THT]"]
  VOL1 = TRIMPOT [package=trim_pot_pth]
  TEMPO = Rotary Potentiometer (Small) [maximum_resistance=100kΩ package=THT]
  S13 = Pushbutton [package="[THT]"]
  S14 = Pushbutton [package="[THT]"]
  B = SWITCH-MOMENTARY-2 [package=tactile-pth-12mm]
  ULN2803 = ULN2803A [package=THT]
  SYNC_IN = Audio Jack (TRS) 3.5mm [package="4Ucon 08780 [THT]"]
  SYNC_OUT = Audio Jack (TRS) 3.5mm [package="4Ucon 08780 [THT]"]
  S10 = Pushbutton [package="[THT]"]
  R4 = Resistor [tolerance=±5% resistance=220 package=THT]
  LED1 = LED - 5mm [color="Red (633nm)" package="5 mm [THT]"]
  LED2 = LED - 5mm [color="Red (633nm)" package="5 mm [THT]"]
  LED3 = LED - 5mm [color="Red (633nm)" package="5 mm [THT]"]
  LED4 = LED - 5mm [color="Red (633nm)" package="5 mm [THT]"]
  R5 = Resistor [tolerance=±5% resistance=220 package=THT]
  R6 = Resistor [tolerance=±5% resistance=220 package=THT]
  R7 = Resistor [tolerance=±5% resistance=220 package=THT]
  J1 = Screw terminal - 2 pins [package=THT]
  J2 = Screw terminal - 2 pins [package=THT]
  J3 = Screw terminal - 2 pins [package=THT]
  J4 = Screw terminal - 2 pins [package=THT]
  Power_plug1 = Power plug
  D1 = Rectifier Diode [part_number=1N4001 package="300 mil [THT]"]
  R8 = Resistor [tolerance=±5% resistance=220 package=THT]
  R9 = Resistor [tolerance=±5% resistance=220 package=THT]
  R10 = Resistor [tolerance=±5% resistance=220 package=THT]
  R11 = Resistor [tolerance=±5% resistance=220 package=THT]
  LED8 = LED - 3mm [color="Green (570nm)" package="3 mm [THT]"]
  LED7 = LED - 3mm [color="Green (570nm)" package="3 mm [THT]"]
  LED6 = LED - 3mm [color="Green (570nm)" package="3 mm [THT]"]
  LED5 = LED - 3mm [color="Green (570nm)" package="3 mm [THT]"]
  Part2 = Arduino Mega 2560 (Rev3)
  D69 = Rectifier Diode [part_number=1N4001 package="300 mil [THT]"]

nets:
  GND: ▼.Pin_1, ▼.Pin_2, A.2, ▲.Pin_1, ▲.Pin_2, LCD1.VSS, LCD1.LED-, S8.Pin_1, S8.Pin_2, ◄.Pin_1, ◄.Pin_2, ►.Pin_1, ►.Pin_2, VOL1.CW, TEMPO.leg1, S13.Pin_1, S13.Pin_2, S14.Pin_1, S14.Pin_2, B.2, ULN2803.0V, SYNC_IN.Sleeve, SYNC_OUT.Sleeve, S10.Pin_1, S10.Pin_2, R4.Pin_1, R5.Pin_1, R6.Pin_1, R7.Pin_1, Power_plug1.GND, R8.Pin_1, R9.Pin_1, R10.Pin_1, R11.Pin_1, Part2.GND, D69.anode
  N1: ▼.Pin_3, ▼.Pin_4, Part2.A13
  N2: A.1, Part2.A3
  N3: ▲.Pin_3, ▲.Pin_4, Part2.A9
  VDD: LCD1.VDD, R2.Pin_1, VOL1.CCW, TEMPO.leg2, J1.pin1, J4.pin1, Part2.5V
  N4: LCD1.V0, VOL1.WIPER
  N5: LCD1.RS, Part2.D10_PWM
  N6: LCD1.R/W, Part2.D9_PWM
  N7: LCD1.E, Part2.D8_PWM
  N8: LCD1.DB4, Part2.D6_PWM
  N9: LCD1.DB5, Part2.D5_PWM
  N10: LCD1.DB6, Part2.D4_PWM
  N11: LCD1.DB7, Part2.D3_PWM
  N12: LCD1.LED+, R2.Pin_0
  N13: S8.Pin_3, S8.Pin_4, Part2.D51
  N14: ◄.Pin_3, ◄.Pin_4, Part2.A8
  N15: ►.Pin_3, ►.Pin_4, Part2.A14
  N16: TEMPO.wiper, Part2.A0
  N17: S13.Pin_3, S13.Pin_4, Part2.D49
  N18: S14.Pin_3, S14.Pin_4, Part2.D47
  N19: B.1, Part2.A2
  N20: ULN2803.In_1, ULN2803.In_2, LED8.anode, Part2.D33
  N21: ULN2803.In_3, ULN2803.In_4, LED7.anode, Part2.D31
  N22: ULN2803.In_5, ULN2803.In_6, LED6.anode, Part2.D29
  N23: ULN2803.In_7, ULN2803.In_8, LED5.anode, Part2.D27
  N24: ULN2803.COM_-_Common, J2.pin1, J3.pin1, D1.cathode, Part2.VIN
  N25: ULN2803.Out_8, ULN2803.Out_7, J2.pin2
  N26: ULN2803.Out_6, ULN2803.Out_5, J3.pin2
  N27: ULN2803.Out_4, ULN2803.Out_3, J4.pin2
  N28: ULN2803.Out_2, ULN2803.Out_1, J1.pin2
  N29: SYNC_IN.Tip, Part2.D25, D69.cathode
  N30: SYNC_OUT.Tip, Part2.D37
  N31: S10.Pin_3, S10.Pin_4, Part2.D53
  N32: R4.Pin_0, LED1.cathode
  N33: LED1.anode, Part2.D45
  N34: LED2.cathode, R5.Pin_0
  N35: LED2.anode, Part2.D43
  N36: LED3.cathode, R6.Pin_0
  N37: LED3.anode, Part2.D41
  N38: LED4.cathode, R7.Pin_0
  N39: LED4.anode, Part2.D39
  N40: Power_plug1.VCC, D1.anode
  N41: R8.Pin_0, LED5.cathode
  N42: R9.Pin_0, LED6.cathode
  N43: R10.Pin_0, LED7.cathode
  N44: R11.Pin_0, LED8.cathode

notes:
  5V
  12V
  1
  2
  3
  4
  -  +
  (1&2)
  (3&4)
